# Fritzing sketch Arduino Temp Controller - Updated 20190416 (saved by Fritzing 0.9.3b)

parts:
  Part1 = Arduino Uno (Rev3)  # not connected
  Part3 = Arduino Prototyping Shield
  Part4 = DeuLigne 1.1 - The Snootlab's LCD shield for Arduino
  J3 = Screw terminal - 2 pins [package=THT]
  J4 = Screw terminal - 2 pins [package=THT]
  Q2 = MOSFET-NCHANNEL [package=to220v]
  R2 = Resistor [tolerance=±5% resistance=150 package=THT]
  Heating_Resistor_2 = Resistor [tolerance=±5% resistance=0.2 package=THT]
  Heating_Resistor_1 = Resistor [tolerance=±5% resistance=0.2 package=THT]
  R3 = Temperature Sensor (Thermistor) [thermistor_type=NTC part_number="10k NTC" package=THT]
  R4 = Resistor [tolerance=±5% resistance=10k package=THT]

nets:
  N1: Part3.+9V, Part3.N$87, J3.pin1, Heating_Resistor_1.Pin_0
  N2: Part3.GND, Part3.N$93, Part3.N$243, Q2.S, R3.pin_0
  N3: Part3.AREF, Part3.3.3V, Part3.N$278, R4.Pin_0
  N4: Part3.D3, Part3.N$421, R2.Pin_1
  N5: Part3.A0, Part3.N$372
  N6: Part3.N$67, J3.pin2, Heating_Resistor_1.Pin_1
  N7: Part3.N$242, Part3.N$405, J4.pin1, Q2.D, Heating_Resistor_2.Pin_0
  N8: Part3.N$368, Part3.N$374, R3.pin_1, R4.Pin_1
  N9: Part3.N$403, J4.pin2, Heating_Resistor_2.Pin_1
  N10: Part3.N$415, Part3.N$418, Q2.G, R2.Pin_0
  N11: Part4.A0, Part4.A5(CLK)
